# Fritzing sketch bras robotisee (saved by Fritzing 0.9.4)
breadboards: 1

parts:
  Part1 = Arduino Nano (Rev3.0)
  J1 = Basic Servo
  J3 = Basic Servo
  J4 = Basic Servo

nets:
  GND: Part1.GND, J1.gnd, J3.gnd, J4.gnd
  N1: Part1.D7, J3.pulse
  N2: Part1.D8, J4.pulse
  N3: Part1.D9, J1.pulse
  VCC: Part1.5V, J1.vcc, J3.vcc, J4.vcc
