# Fritzing sketch bras_robot_boutons (saved by Fritzing 0.9.4)
breadboards: 1

parts:
  Part2 = Arduino Nano (Rev3.0)
  S1 = Pushbutton [package="[THT]"]
  S2 = Pushbutton [package="[THT]"]
  S3 = Pushbutton [package="[THT]"]

nets:
  N1: Part2.5V, S1.Pin_3, S1.Pin_4, S2.Pin_3, S2.Pin_4, S3.Pin_3, S3.Pin_4
  N2: Part2.A2, S3.Pin_1, S3.Pin_2
  N3: Part2.A1, S2.Pin_1, S2.Pin_2
  N4: Part2.A0, S1.Pin_1, S1.Pin_2
