# Fritzing sketch moteur_emile (saved by Fritzing 0.9.4)
breadboards: 1

parts:
  Part3 = Arduino Nano (Rev3.0)
  J1 = Basic Servo
  NEOPIXEL1 = Neopixel Strip -- Black (60/m) [part_number=1461]
  Part4 = ultrasonic
  S1 = Pushbutton [package="[THT]"]

nets:
  GND: Part3.GND, J1.gnd, NEOPIXEL1.GND, Part4.GND
  N1: Part3.D2, Part4.Echo
  N2: Part3.D3, Part4.Trig
  N3: Part3.D9, J1.pulse
  VCC: Part3.5V, J1.vcc, NEOPIXEL1.+5V, Part4.VCC, S1.Pin_3, S1.Pin_4
  N4: Part3.A1, S1.Pin_1, S1.Pin_2
  N5: Part3.A0, NEOPIXEL1.DO

custom parts:
  Neopixel Strip -- Black (60/m): Neopixel Strip, Black, 60 pixels per meter.
